# Fritzing sketch Joystick (saved by Fritzing 0.9.6b)
breadboards: 1

parts:
  R1 = Resistor [tolerance=±5% resistance=330 package="0402 [SMD]"]
  LED1 = LED - 5mm [color="Green (555nm)" current=0.030 package="5 mm [THT]"]
  Componente1 = Arduino Uno (Rev3) - ICSP
  Componente2 = Thumb Joystick
  LED2 = LED - 5mm [color="Green (555nm)" current=0.030 package="5 mm [THT]"]
  R2 = Resistor [tolerance=±5% resistance=330 package="0402 [SMD]"]
  LED3 = LED - 5mm [color="Yellow (595nm)" current=0.030 package="5 mm [THT]"]
  R3 = Resistor [tolerance=±5% resistance=330 package="0402 [SMD]"]
  R4 = Resistor [tolerance=±5% resistance=330 package="0402 [SMD]"]
  LED4 = LED - 5mm [color="Red (633nm)" current=0.030 package="5 mm [THT]"]
  LED5 = LED - 5mm [color="Red (633nm)" current=0.030 package="5 mm [THT]"]
  R5 = Resistor [tolerance=±5% resistance=330 package="0402 [SMD]"]
  R6 = Resistor [tolerance=±5% resistance=10k package="0402 [SMD]"]

nets:
  N1: R1.Pin_0, LED1.anode
  N2: R1.Pin_1, Componente1.D9_PWM
  N3: LED1.cathode, Componente2.GND, LED2.cathode, LED3.cathode, LED4.cathode, LED5.cathode
  N4: Componente1.A0, Componente2.VERT
  N5: Componente1.A1, Componente2.HORZ
  N6: Componente1.ICSP_MOSI, Componente1.D11_PWM/MOSI, R3.Pin_1
  N7: Componente1.D10_PWM/SS, Componente2.SEL, R6.Pin_0
  N8: Componente1.D3_PWM, R5.Pin_1
  N9: Componente1.D5_PWM, R4.Pin_1
  N10: Componente1.D6_PWM, R2.Pin_1
  N11: Componente2.VCC, R6.Pin_1
  N12: LED2.anode, R2.Pin_0
  N13: LED3.anode, R3.Pin_0
  N14: R4.Pin_0, LED4.anode
  N15: LED5.anode, R5.Pin_0
